# Fritzing sketch pcb_Test (saved by Fritzing 0.9.3b)
circuit board: 8.46667cm x 5.64444cm
breadboards: 1

parts:
  Part1 = Arduino Nano (Rev3.0)
  U1 = 74HC04_HEX_INVERTER [package=dil14]
  U2 = 74HC04_HEX_INVERTER [package=dil14]
  JP1 = Header 5x2 [package=2x5-shrouded_smd]
  JP2 = Header 5x2 [package=2x5-shrouded_smd]

nets:
  N1: Part1.D2, U1.3Y
  N2: Part1.D3, U1.3A
  N3: Part1.D4, U1.2A
  N4: U1.1Y, JP2.10
  N5: U1.GND, U2.3A
  N6: U1.4Y, U2.4Y, JP1.5, JP2.5
  N7: U1.4A, JP2.3
  N8: U1.5Y, JP2.1
  N9: U1.5A, JP2.2
  N10: U1.6Y, JP2.4
  N11: U1.6A, JP2.6
  N12: U1.VCC, JP2.8
  N13: U2.1Y, JP1.10
  N14: U2.4A, JP1.3
  N15: U2.5Y, JP1.1
  N16: U2.5A, JP1.2
  N17: U2.6Y, JP1.4
  N18: U2.6A, JP1.6
  N19: U2.VCC, JP1.8
